# Fritzing sketch servo_sweep (saved by Fritzing 1.0.4)
stripboards: 1

parts:
  Part1 = Arduino Nano (Rev3.0)
  VCC1 = Battery
  C1 = Film/Foil Capacitor [capacitance=100nF voltage=35V package="7.5mm [THT, pp]"]
  C2 = Ceramic Capacitor [capacitance=100nF voltage=35V package="100 mil [THT, multilayer]"]
  U1 = POT [knob_status=50% power=0.5W package=alps_pot]
  J1 = Dagu DGServo 9g header connector (female) [package=THT]
  C3 = Electrolytic Capacitor [capacitance=2.2mF voltage=35V package="100 mil [THT, electrolytic]"]
  U2 = Voltage Regulator - 5V [package="TO220 [THT]"]

nets:
  GND: Part1.GND, VCC1.-, C1.-, C2.0, U1.A, J1.gnd, C3.-, U2.GND
  N1: Part1.D9, U1.S
  5V: Part1.5V, C2.1, U1.E, J1.Vcc, C3.+, U2.output_voltage
  N2: Part1.A0, J1.pulse
  N3: VCC1.+, C1.+, U2.input_voltage

custom parts:
  Battery: Your standard 2x 18650 battery pack (7,4 Volts)
